# Fritzing sketch Project 2 (saved by Fritzing 0.9.3b)

parts:
  MD1 = Maker Drive
  Raspberry_Pi_1 = Raspberry Pi 3 [part_number=RPI-3-V1.2]
  M1 = DC Motor  # not connected
  M2 = DC Motor  # not connected
  BATT1 = 4xAA Switchable Battery Pack w/Bare Wire

nets:
  N1: MD1.VB+, BATT1.POS
  N2: MD1.VB-, BATT1.NEG
  N3: MD1.M1A_IO, Raspberry_Pi_1.GPIO17
  N4: MD1.M1B_IO, Raspberry_Pi_1.GPIO27
  N5: MD1.M2A_IO, Raspberry_Pi_1.GPIO23
  N6: MD1.M2B_IO, Raspberry_Pi_1.GPIO24

custom parts:
  Maker Drive: Simplifying H-Bridge Motor Driver for Beginner.
  4xAA Switchable Battery Pack w/Bare Wire: 4xAA Switchable Battery Pack with Bare Wire connection
